# Fritzing sketch weatherClock (saved by Fritzing 0.9.2b)

parts:
  R1 = Resistor [tolerance=±5% resistance=220 package=THT]
  R3 = Resistor [tolerance=±5% resistance=220 package=THT]
  R4 = Resistor [tolerance=±5% resistance=220 package=THT]
  DI1 = 4位共阴数码管 [package=THT]
  元件1 = Arduino Uno (Rev3)
  R2 = Resistor [tolerance=±5% resistance=220 package=THT]

nets:
  N1: R1.Pin_0, 元件1.D11_PWM/MOSI
  N2: R1.Pin_1, DI1.com2
  N3: R3.Pin_0, DI1.com4
  N4: R3.Pin_1, 元件1.D13/SCK
  N5: R4.Pin_0, 元件1.D10_PWM/SS
  N6: R4.Pin_1, DI1.com1
  N7: DI1.cathodeE, 元件1.D6_PWM
  N8: DI1.cathodeD, 元件1.D5_PWM
  N9: DI1.cathodeC, 元件1.D4
  N10: DI1.cathodeDP, 元件1.D9_PWM
  N11: DI1.cathodeB, 元件1.D3_PWM
  N12: DI1.cathodeA, 元件1.D2
  N13: DI1.cathodeF, 元件1.D7
  N14: DI1.cathodeG, 元件1.D8
  N15: DI1.com3, R2.Pin_1
  N16: 元件1.D12/MISO, R2.Pin_0
